// Logisim project faerie.circ as structural Verilog: 4 circuits, main circuit main
module main (
);

  wire alu_1_cout, and_1_out, and_2_out, and_3_out, and_4_out, and_5_out, and_6_out, and_7_out, and_8_out,
       and_9_out, and_10_out, and_11_out, and_12_out, and_13_out, and_14_out, and_15_out, and_16_out,
       button_1_out, clock_1_out, comparator_1_eq, comparator_2_eq, comparator_3_eq,
       control_unit_1_async_reset_b, control_unit_1_branch, control_unit_1_increment_al,
       control_unit_1_memory_read, control_unit_1_memory_write, control_unit_1_pc_as_address,
       control_unit_1_set_ah, control_unit_1_set_al, control_unit_1_write_a, control_unit_1_write_fr,
       control_unit_1_zero_page_address, multiplexer_2_out, not_1_out, not_2_out, not_3_out, or_2_out,
       or_3_out, xor_3_out, ZF_q;
  wire [0:0] or_1_out;
  wire [1:0] CF_q;
  wire [3:0] control_unit_1_mode_select;
  wire [4:0] bit_extender_4_out;
  wire [7:0] A_2_out, A_q, AH_q, AL_q, alu_1_q, B_q, bit_extender_1_out, cmo_8x32_led_matrix_driver_1_out_5,
       cmo_8x32_led_matrix_driver_1_out_6, cmo_8x32_led_matrix_driver_1_out_7,
       cmo_8x32_led_matrix_driver_1_out_8, cmo_8x32_led_matrix_driver_1_out_9,
       cmo_8x32_led_matrix_driver_1_out_10, cmo_8x32_led_matrix_driver_1_out_11,
       cmo_8x32_led_matrix_driver_1_out_12, cmo_8x32_led_matrix_driver_1_out_13,
       cmo_8x32_led_matrix_driver_1_out_14, cmo_8x32_led_matrix_driver_1_out_15,
       cmo_8x32_led_matrix_driver_1_out_16, cmo_8x32_led_matrix_driver_1_out_17,
       cmo_8x32_led_matrix_driver_1_out_18, cmo_8x32_led_matrix_driver_1_out_19,
       cmo_8x32_led_matrix_driver_1_out_20, cmo_8x32_led_matrix_driver_1_out_21,
       cmo_8x32_led_matrix_driver_1_out_22, cmo_8x32_led_matrix_driver_1_out_23,
       cmo_8x32_led_matrix_driver_1_out_24, cmo_8x32_led_matrix_driver_1_out_25,
       cmo_8x32_led_matrix_driver_1_out_26, cmo_8x32_led_matrix_driver_1_out_27,
       cmo_8x32_led_matrix_driver_1_out_28, cmo_8x32_led_matrix_driver_1_out_29,
       cmo_8x32_led_matrix_driver_1_out_30, cmo_8x32_led_matrix_driver_1_out_31,
       cmo_8x32_led_matrix_driver_1_out_32, cmo_8x32_led_matrix_driver_1_out_33,
       cmo_8x32_led_matrix_driver_1_out_34, cmo_8x32_led_matrix_driver_1_out_35,
       cmo_8x32_led_matrix_driver_1_out_36, controlled_buffer_2_out, nor_1_out, rom_1_data;
  wire [13:0] bit_extender_2_out;
  wire [14:0] bit_extender_3_out;
  wire [15:0] multiplexer_1_out, PC_q, RA_q, xor_1_out, xor_2_out;

  assign bit_extender_1_out = {{7{control_unit_1_zero_page_address}}, control_unit_1_zero_page_address};  // Bit_Extender bit_extender_1
  and and_1 (and_1_out, and_6_out, control_unit_1_branch);
  Bit_Extender #(.in_width(16), .out_width(14)) bit_extender_2 (.in(multiplexer_1_out), .out(bit_extender_2_out));
  Bit_Extender #(.in_width(16), .out_width(15)) bit_extender_3 (.in(multiplexer_1_out), .out(bit_extender_3_out));
  and and_2 (and_2_out, control_unit_1_memory_read, multiplexer_1_out[14], multiplexer_1_out[15]);
  assign xor_1_out = 16'hc000 ^ {nor_1_out, AL_q[7:1], or_1_out[0]};  // XOR_Gate xor_1, 16 bits wide
  and and_3 (and_3_out, or_3_out, control_unit_1_branch);
  and and_4 (and_4_out, not_1_out, control_unit_1_memory_write);
  and and_5 (and_5_out, not_1_out, control_unit_1_memory_read);
  not not_1 (not_1_out, multiplexer_1_out[15]);
  Counter #(.width(16), .max('hffff)) PC (
    .load(and_3_out), .D(xor_1_out), .count(control_unit_1_pc_as_address), .Q(PC_q), .clk(clock_1_out),
    .clr(button_1_out));  // open: carry
  not not_2 (not_2_out, control_unit_1_pc_as_address);
  Register AH (.D(controlled_buffer_2_out), .en(control_unit_1_set_ah), .Q(AH_q), .clk(clock_1_out));  // open: clr
  Register AL (.D(controlled_buffer_2_out), .en(control_unit_1_set_al), .Q(AL_q), .clk(clock_1_out));  // open: clr
  ROM #(.addrWidth(14)) rom_1 (.addr(bit_extender_2_out), .data(rom_1_data), .sel(and_2_out));
  RAM #(.addrWidth(15), .bus("separate")) ram_1 (
    .addr(bit_extender_3_out), .din(rom_1_data), .data(rom_1_data), .str(and_4_out), .clk(clock_1_out),
    .ld(and_5_out));  // open: sel, clr
  assign xor_2_out = 16'hc000 ^ PC_q;  // XOR_Gate xor_2, 16 bits wide
  Multiplexer #(.width(16), .enable("false")) multiplexer_1 (
    .in0(xor_2_out), .in1({nor_1_out, AL_q[7:1], or_1_out[0]}), .out(multiplexer_1_out), .sel(not_2_out));
  assign nor_1_out = ~(~AH_q | bit_extender_1_out);  // NOR_Gate nor_1, 8 bits wide
  or or_1 (or_1_out[0], control_unit_1_increment_al, AL_q[0]);
  control_unit control_unit_1 (
    .Data_bus(controlled_buffer_2_out), .Mode_select(control_unit_1_mode_select),
    .Memory_write(control_unit_1_memory_write), .Memory_read(control_unit_1_memory_read),
    .Branch(control_unit_1_branch), .PC_as_address(control_unit_1_pc_as_address),
    .Set_AL(control_unit_1_set_al), .Set_AH(control_unit_1_set_ah),
    .Zero_page_address(control_unit_1_zero_page_address), .Clock(clock_1_out), .Reset(button_1_out),
    .Async_reset_B(control_unit_1_async_reset_b), .Write_FR(control_unit_1_write_fr),
    .Write_A(control_unit_1_write_a), .Increment_AL(control_unit_1_increment_al));
  // Probe on multiplexer_1_out
  // Probe on rom_1_data
  Clock clock_1 (.out(clock_1_out));
  and and_6 (and_6_out, control_unit_1_mode_select[0], control_unit_1_mode_select[3]);
  Bit_Extender #(.in_width(16), .out_width(5)) bit_extender_4 (.in(multiplexer_1_out), .out(bit_extender_4_out));
  and and_7 (and_7_out, ~multiplexer_1_out[12], ~multiplexer_1_out[13], and_8_out);  // AND_Gate
  and and_8 (and_8_out, ~multiplexer_1_out[14], multiplexer_1_out[15]);  // AND_Gate
  Comparator #(.width(16)) comparator_1 (.a(multiplexer_1_out), .b(16'h9000), .eq(comparator_1_eq));  // open: gt, lt
  Button button_1 (.out(button_1_out));
  LED led_1 (.in(control_unit_1_memory_read));
  LED led_2 (.in(control_unit_1_memory_write));
  assign rom_1_data = control_unit_1_memory_write ? A_q : 8'bz;  // Controlled_Buffer controlled_buffer_1
  assign controlled_buffer_2_out = not_3_out ? rom_1_data : 8'bz;  // Controlled_Buffer controlled_buffer_2
  assign controlled_buffer_2_out = and_13_out ? RA_q[7:0] : 8'bz;  // Controlled_Buffer controlled_buffer_3
  Register #(.width(16)) RA (.D(xor_2_out), .en(and_1_out), .Q(RA_q), .clk(clock_1_out), .clr(button_1_out));
  Register A (.D(alu_1_q), .en(control_unit_1_write_a), .Q(A_q), .clk(clock_1_out), .clr(button_1_out));
  Register B (
    .D(controlled_buffer_2_out), .en(control_unit_1_memory_read), .Q(B_q), .clk(clock_1_out),
    .clr(control_unit_1_async_reset_b));
  DotMatrix #(.matrixcols(32), .matrixrows(8)) dotmatrix_1 (
    .col0(cmo_8x32_led_matrix_driver_1_out_5), .col1(cmo_8x32_led_matrix_driver_1_out_9),
    .col2(cmo_8x32_led_matrix_driver_1_out_13), .col3(cmo_8x32_led_matrix_driver_1_out_17),
    .col4(cmo_8x32_led_matrix_driver_1_out_21), .col5(cmo_8x32_led_matrix_driver_1_out_25),
    .col6(cmo_8x32_led_matrix_driver_1_out_29), .col7(cmo_8x32_led_matrix_driver_1_out_33),
    .col8(cmo_8x32_led_matrix_driver_1_out_6), .col9(cmo_8x32_led_matrix_driver_1_out_10),
    .col10(cmo_8x32_led_matrix_driver_1_out_14), .col11(cmo_8x32_led_matrix_driver_1_out_18),
    .col12(cmo_8x32_led_matrix_driver_1_out_22), .col13(cmo_8x32_led_matrix_driver_1_out_26),
    .col14(cmo_8x32_led_matrix_driver_1_out_30), .col15(cmo_8x32_led_matrix_driver_1_out_34),
    .col16(cmo_8x32_led_matrix_driver_1_out_7), .col17(cmo_8x32_led_matrix_driver_1_out_11),
    .col18(cmo_8x32_led_matrix_driver_1_out_15), .col19(cmo_8x32_led_matrix_driver_1_out_19),
    .col20(cmo_8x32_led_matrix_driver_1_out_23), .col21(cmo_8x32_led_matrix_driver_1_out_27),
    .col22(cmo_8x32_led_matrix_driver_1_out_31), .col23(cmo_8x32_led_matrix_driver_1_out_35),
    .col24(cmo_8x32_led_matrix_driver_1_out_8), .col25(cmo_8x32_led_matrix_driver_1_out_12),
    .col26(cmo_8x32_led_matrix_driver_1_out_16), .col27(cmo_8x32_led_matrix_driver_1_out_20),
    .col28(cmo_8x32_led_matrix_driver_1_out_24), .col29(cmo_8x32_led_matrix_driver_1_out_28),
    .col30(cmo_8x32_led_matrix_driver_1_out_32), .col31(cmo_8x32_led_matrix_driver_1_out_36));
  and and_9 (and_9_out, control_unit_1_memory_write, and_7_out);
  CMO_8x32_LED_matrix_driver cmo_8x32_led_matrix_driver_1 (
    .write_enable(and_9_out), .address(bit_extender_4_out), .write_data(rom_1_data),
    .out_5(cmo_8x32_led_matrix_driver_1_out_5), .out_6(cmo_8x32_led_matrix_driver_1_out_6),
    .out_7(cmo_8x32_led_matrix_driver_1_out_7), .out_8(cmo_8x32_led_matrix_driver_1_out_8),
    .out_9(cmo_8x32_led_matrix_driver_1_out_9), .out_10(cmo_8x32_led_matrix_driver_1_out_10),
    .out_11(cmo_8x32_led_matrix_driver_1_out_11), .out_12(cmo_8x32_led_matrix_driver_1_out_12),
    .out_13(cmo_8x32_led_matrix_driver_1_out_13), .out_14(cmo_8x32_led_matrix_driver_1_out_14),
    .out_15(cmo_8x32_led_matrix_driver_1_out_15), .out_16(cmo_8x32_led_matrix_driver_1_out_16),
    .out_17(cmo_8x32_led_matrix_driver_1_out_17), .out_18(cmo_8x32_led_matrix_driver_1_out_18),
    .out_19(cmo_8x32_led_matrix_driver_1_out_19), .out_20(cmo_8x32_led_matrix_driver_1_out_20),
    .out_21(cmo_8x32_led_matrix_driver_1_out_21), .out_22(cmo_8x32_led_matrix_driver_1_out_22),
    .out_23(cmo_8x32_led_matrix_driver_1_out_23), .out_24(cmo_8x32_led_matrix_driver_1_out_24),
    .out_25(cmo_8x32_led_matrix_driver_1_out_25), .out_26(cmo_8x32_led_matrix_driver_1_out_26),
    .out_27(cmo_8x32_led_matrix_driver_1_out_27), .out_28(cmo_8x32_led_matrix_driver_1_out_28),
    .out_29(cmo_8x32_led_matrix_driver_1_out_29), .out_30(cmo_8x32_led_matrix_driver_1_out_30),
    .out_31(cmo_8x32_led_matrix_driver_1_out_31), .out_32(cmo_8x32_led_matrix_driver_1_out_32),
    .out_33(cmo_8x32_led_matrix_driver_1_out_33), .out_34(cmo_8x32_led_matrix_driver_1_out_34),
    .out_35(cmo_8x32_led_matrix_driver_1_out_35), .out_36(cmo_8x32_led_matrix_driver_1_out_36),
    .clock(clock_1_out));
  Button button_2 (.out(A_2_out[7]));
  and and_10 (and_10_out, comparator_1_eq, button_1_out);
  assign rom_1_data = and_10_out ? A_2_out : 8'bz;  // Controlled_Buffer controlled_buffer_4
  not not_3 (not_3_out, comparator_3_eq);
  assign controlled_buffer_2_out = and_11_out ? {{6{1'b0}}, CF_q} : 8'bz;  // Controlled_Buffer controlled_buffer_5
  and and_11 (and_11_out, comparator_3_eq, multiplexer_1_out[1]);
  assign controlled_buffer_2_out = and_12_out ? RA_q[15:8] : 8'bz;  // Controlled_Buffer controlled_buffer_6
  and and_12 (and_12_out, comparator_3_eq, ~multiplexer_1_out[1], multiplexer_1_out[0]);  // AND_Gate
  and and_13 (and_13_out, comparator_3_eq, ~multiplexer_1_out[1], ~multiplexer_1_out[0]);  // AND_Gate
  ALU alu_1 (
    .Cin(CF_q[0]), .A(A_q), .B(B_q), .Cout(alu_1_cout), .Q(alu_1_q), .CC(control_unit_1_mode_select[3]),
    .SUB_AND(control_unit_1_mode_select[2]), .SHL_XOR(control_unit_1_mode_select[1]),
    .LOGIC_B(control_unit_1_mode_select[0]));
  Register #(.width(1)) CF (
    .D(alu_1_cout), .en(control_unit_1_write_fr), .Q(CF_q[0]), .clk(clock_1_out), .clr(button_1_out));
  and and_14 (and_14_out, ~ZF_q, ~CF_q[0]);  // AND_Gate
  Button button_3 (.out(A_2_out[4]));
  Button button_4 (.out(A_2_out[6]));
  Button v (.out(A_2_out[5]));
  or or_2 (or_2_out, ~control_unit_1_mode_select[3], ZF_q);  // OR_Gate
  Comparator comparator_2 (.a(alu_1_q), .b({8{1'b0}}), .eq(comparator_2_eq));  // open: gt, lt
  and and_15 (and_15_out, CF_q[0], ~ZF_q);  // AND_Gate
  Button SELECT (.out(A_2_out[2]));
  Button START (.out(A_2_out[3]));
  Comparator #(.width(13)) comparator_3 (
    .a(multiplexer_1_out[15:3]), .b({13{1'b0}}), .eq(comparator_3_eq));  // open: gt, lt
  Register #(.width(1)) ZF (
    .D(and_16_out), .en(control_unit_1_write_fr), .Q(ZF_q), .clk(clock_1_out), .clr(button_1_out));
  and and_16 (and_16_out, or_2_out, comparator_2_eq);
  Multiplexer #(.select(2), .enable("false")) multiplexer_2 (
    .in0(ZF_q), .in1(CF_q[0]), .in2(and_15_out), .in3(and_14_out), .out(multiplexer_2_out),
    .sel(control_unit_1_mode_select[1:0]));
  xor xor_3 (xor_3_out, multiplexer_2_out, control_unit_1_mode_select[2]);
  or or_3 (or_3_out, xor_3_out, control_unit_1_mode_select[3]);
  Button A_2 (.out(A_2_out[0]));
  Button B_2 (.out(A_2_out[1]));
  not not_4 (CF_q[1], ZF_q);

  // Notes on the sheet:
  //   contents of rom_1 (hex, n*v repeats v):
  //   8b fb c2 5c 0 2 90 5c 80 2 91 8b 54 c0 6d 20 6b 5d c0 6d 7f 7b 5d c0 2 92 c c c 60 92 2c 69 2 92 5c
  //   0 ac c0 2 92 5c 0 2 94 54 92 6 90 50 92 2c 1 2 92 50 93 ac 0 2 93 50 90 2c 1 2 90 50 91 ac 0 2 91 50
  //   94 2c 1 2 94 6d 7 3b 2d c0 50 80 6d 0 4b e c0 87 0 50 90 2c 7 2 90 50 91 ac 0 2 91 0 0 0 8 5*0 4 0
  //   10 0 0 0 2 4 8 10 20 0 0 2 4 8 10 20 0 0 2 4 8 10 20 0 0 2 4 8 10 20 4*0 8 5*0 4 8 6*0 8 10 0 0 0 2
  //   4 8 10 20 0 0 2 4 8 10 20 0 0 0 4 8 4*0 2 4 8 10 20 4*0 8 5*0 4 8 10 0 0 0 2 4 8 10 20 0 0 2 4 8 10
  //   20 0 0 2 4 8 10 20 0 0 2 4 8 10 20 0 0 2 4 8 10 20 0 0 2 4 8 10 20 0 0 2 4 8 10 20 0 0 2 4 8 10 20 0
  //   0 2 4 8 10 20 0 0 2 4 8 10 20 4*0 8 5*0 4 8 5*0 4 8 10 0 0 0 2 4 8 10 20 0 0 0 4 8 10 0 0 0 2 4 8 10
  //   20 0 0 2 4 8 10 20 0 0 2 4 8 10 20 0 0 2 4 8 10 20 0 0 2 4 8 10 20 0 0 2 4 8 10 20 0 0 2 4 8 10 20 0
  //   0 2 4 8 10 20 0 0 2 4 8 10 20 0 0 2 4 8 10 20 0 0 2 4 8 10 20 0 0 2 4 8 10 20 0 0 2 4 8 10 20 0 0 2
  //   4 8 10 20 0 0 2 4 8 10 20 0 0 2 4 8 10 20 0 0 2 4 8 10 20 0 0 2 4 8 10 20 0 0 2 4 8 10 20 0 0 2 4 8
  //   10 20 0 0 2 4 8 10 20 0 0 2 4 8 10 20 0 0 2 4 8 10 20 0 0 2 4 8 10 20 0 0 2 4 8 10 20 0 0 2 4 8 10
  //   20 0 0 2 4 8 10 20 0 0 2 4 8 10 20 0 0 0 4 8 10 4*0 4 8 10 4*0 4 8 10 0 0 0 2 4 8 10 20 0 0 2 4 8 10
  //   20 0 0 0 4 8 4*0 2 4 8 10 20 0 0 2 4 8 10 20 0 0 2 4 8 10 20 0 0 2 4 8 10 20 0 0 2 4 8 10 20 0 0 2 4
  //   8 10 0 0 0 2 4 8 10 20 0 0 2 4 8 10 20 0 0 0 4 8 10 4*0 4 8 4*0 2 4 8 10 4*0 4 8 10 0 0 0 2 4 8 10
  //   20 0 0 2 4 8 10 20 0 0 2 4 8 10 20 0 0 2 4 8 10 20 0 0 2 4 8 10 20 0 0 2 4 8 10 20 0 0 2 4 8 10 20 0
  //   0 0 4 8 10 0 0 0 2 4 8 10 20 0 0 2 4 8 10 20 0 0 2 4 8 10 20 0 0 2 4 8 10 20 0 0 2 4 8 10 20 0 0 2 4
  //   8 10 20 0 0 2 4 8 10 5*0 8 5*0 4 8 10 20 0 0 2 4 8 10 20 40 5c 0 a 0 80 a 1 80 a 2 80 a 3 80 a 4 80
  //   a 5 80 a 6 80 a 7 80 a 8 80 a 9 80 a a 80 a b 80 a c 80 a d 80 a e 80 a f 80 a 10 80 a 11 80 a 12 80
  //   a 13 80 a 14 80 a 15 80 a 16 80 a 17 80 a 18 80 a 19 80 a 1a 80 a 1b 80 a 1c 80 a 1d 80 a 1e 80 a 1f
  //   80 5c 6b 2 80 5c c3 2 81 9b 3 c0 8b 68 c3 48 69 54 68 65 72
endmodule

module control_unit (
  input  [7:0] Data_bus,
  input  Clock,
  input  Reset,
  output Memory_write,
  output Memory_read,
  output Branch,
  output PC_as_address,
  output Set_AL,
  output Set_AH,
  output Zero_page_address,
  output Async_reset_B,
  output Write_FR,
  output Write_A,
  output Increment_AL,
  output [3:0] Mode_select
);

  wire and_2_out, comparator_1_eq, demultiplexer_1_out0, demultiplexer_2_out0, demultiplexer_3_out0,
       demultiplexer_4_out0, demultiplexer_4_out1, demultiplexer_5_out1, nand_1_out, nor_1_out, nor_2_out,
       nor_3_out, not_1_out, or_1_out, or_2_out, or_5_out;
  wire [3:0] multiplexer_1_out;
  wire [5:0] FSM_q;
  wire [7:0] demultiplexer_2_out1, IR_q;

  and and_1 (Async_reset_B, Clock, nor_1_out);
  not not_1 (not_1_out, nor_1_out);
  Register IR (.D(Data_bus), .en(nor_1_out), .Q(IR_q), .clk(Clock), .clr(Reset));
  Multiplexer #(.width(8), .enable("false")) multiplexer_1 (
    .in0(Data_bus), .in1(IR_q), .out({Mode_select, multiplexer_1_out}), .sel(not_1_out));
  Comparator #(.width(4)) comparator_1 (.a(4'b0101), .b(Mode_select), .eq(comparator_1_eq));  // open: gt, lt
  nor nor_1 (nor_1_out, FSM_q[0], FSM_q[1], Increment_AL, FSM_q[3], FSM_q[4], FSM_q[5], Memory_write, Branch);
  Register FSM (
    .D({demultiplexer_2_out1[7:4], Increment_AL, demultiplexer_2_out1[2:0]}),
    .Q({Branch, Memory_write, FSM_q[5:3], Increment_AL, FSM_q[1:0]}), .clk(Clock), .clr(Reset));  // open: en
  nor nor_2 (nor_2_out, Mode_select[0], Mode_select[1]);
  or or_1 (or_1_out, Increment_AL, FSM_q[3], FSM_q[4]);
  or or_2 (or_2_out, nor_1_out, FSM_q[0], FSM_q[1]);
  or or_3 (Memory_read, or_2_out, or_1_out);
  Demultiplexer #(.enable("false")) demultiplexer_1 (
    .out0(demultiplexer_1_out0), .out1(demultiplexer_2_out1[1]), .in(FSM_q[0]), .sel(multiplexer_1_out[3]));
  or or_4 (PC_as_address, or_2_out, and_2_out);
  and and_2 (and_2_out, FSM_q[4], ~nand_1_out);  // AND_Gate
  Demultiplexer #(.enable("false")) demultiplexer_2 (
    .out0(demultiplexer_2_out0), .out1(demultiplexer_2_out1[0]), .in(nor_1_out), .sel(nand_1_out));
  Demultiplexer #(.enable("false")) demultiplexer_3 (
    .out0(demultiplexer_3_out0), .out1(demultiplexer_2_out1[2]), .in(demultiplexer_1_out0),
    .sel(multiplexer_1_out[2]));
  nand nand_1 (nand_1_out, multiplexer_1_out[2], multiplexer_1_out[3]);
  Demultiplexer #(.enable("false")) demultiplexer_4 (
    .out0(demultiplexer_4_out0), .out1(demultiplexer_4_out1), .in(or_5_out), .sel(multiplexer_1_out[1]));
  or or_5 (or_5_out, demultiplexer_2_out0, demultiplexer_3_out0, FSM_q[1], FSM_q[3]);
  nor nor_3 (nor_3_out, multiplexer_1_out[3], multiplexer_1_out[2]);
  and and_3 (Write_FR, FSM_q[5], ~comparator_1_eq);  // AND_Gate
  Demultiplexer #(.enable("false")) demultiplexer_5 (
    .out0(demultiplexer_2_out1[4]), .out1(demultiplexer_5_out1), .in(demultiplexer_4_out0), .sel(nor_2_out));
  Demultiplexer #(.enable("false")) demultiplexer_6 (
    .out0(demultiplexer_2_out1[6]), .out1(demultiplexer_2_out1[7]), .in(demultiplexer_4_out1),
    .sel(multiplexer_1_out[0]));
  or or_6 (Set_AL, FSM_q[0], FSM_q[3]);
  or or_7 (Set_AH, FSM_q[1], Increment_AL);
  or or_8 (Zero_page_address, FSM_q[3], nor_3_out, Increment_AL);
  and and_4 (Write_A, FSM_q[5], ~multiplexer_1_out[0]);  // AND_Gate
  or or_9 (demultiplexer_2_out1[5], demultiplexer_5_out1, FSM_q[4]);

  // Notes on the sheet:
  //   PC_as_address: pull=down
  //   Branch: pull=down
  //   Memory_write: pull=down
  //   Clock: pull=down
  //   Zero_page_address: pull=down
  //   Data_bus: pull=down
  //   Set_AL: pull=down
  //   Mode_select: pull=down
  //   Reset: pull=down
  //   Memory_read: pull=down
  //   Set_AH: pull=down
  //   Insn load
  //   Addr #1
  //   Addr #2
  //   Ptr #1
  //   Ptr #2
  //   Mem load
  //   ALU
  //   Mem store
  //   Branch
  //   Addr #1
  //   Addr #2
  //   Ptr #1
  //   Ptr #2
  //   Mem load
  //   ALU
  //   Mem store
  //   Branch
endmodule

module ALU (
  input  CC,
  input  Cin,
  input  [7:0] A,
  input  [7:0] B,
  input  SUB_AND,
  input  SHL_XOR,
  input  LOGIC_B,
  output Cout,
  output [7:0] Q
);

  wire adder_1_cout, multiplexer_1_out, not_1_out, or_1_out;
  wire [7:0] adder_1_out, bit_extender_1_out, bit_extender_2_out, multiplexer_2_out, multiplexer_3_out,
       multiplexer_5_out, multiplexer_7_out, nor_1_out, xor_1_out, xor_2_out, xor_3_out;
  wire [7:7] and_1_out;

  and and_1 (and_1_out[7], CC, Cin);
  Multiplexer #(.enable("false")) multiplexer_1 (.in0(SUB_AND), .in1(Cin), .out(multiplexer_1_out), .sel(CC));
  not not_1 (not_1_out, SUB_AND);
  Multiplexer #(.width(8), .enable("false")) multiplexer_2 (
    .in0(A), .in1(bit_extender_1_out), .out(multiplexer_2_out), .sel(SHL_XOR));
  assign bit_extender_1_out = {{7{SUB_AND}}, SUB_AND};  // Bit_Extender bit_extender_1
  assign xor_1_out = B ^ multiplexer_2_out;  // XOR_Gate xor_1, 8 bits wide
  assign xor_2_out = A ^ bit_extender_1_out;  // XOR_Gate xor_2, 8 bits wide
  assign bit_extender_2_out = {{7{not_1_out}}, not_1_out};  // Bit_Extender bit_extender_2
  Adder adder_1 (.a(A), .b(xor_1_out), .out(adder_1_out), .cin(multiplexer_1_out), .cout(adder_1_cout));
  assign nor_1_out = ~(xor_1_out | xor_2_out);  // NOR_Gate nor_1, 8 bits wide
  assign xor_3_out = nor_1_out ^ bit_extender_2_out;  // XOR_Gate xor_3, 8 bits wide
  or or_1 (or_1_out, SHL_XOR, not_1_out);
  Multiplexer #(.width(8), .enable("false")) multiplexer_3 (
    .in0(xor_1_out), .in1(xor_3_out), .out(multiplexer_3_out), .sel(SHL_XOR));
  Multiplexer #(.enable("false")) multiplexer_4 (.in0(A[0]), .in1(adder_1_cout), .out(Cout), .sel(or_1_out));
  Multiplexer #(.width(8), .enable("false")) multiplexer_5 (
    .in0({and_1_out[7], A[7:1]}), .in1(B), .out(multiplexer_5_out), .sel(LOGIC_B));
  Multiplexer #(.width(8), .enable("false")) multiplexer_6 (
    .in0(multiplexer_5_out), .in1(multiplexer_7_out), .out(Q), .sel(or_1_out));
  Multiplexer #(.width(8), .enable("false")) multiplexer_7 (
    .in0(adder_1_out), .in1(multiplexer_3_out), .out(multiplexer_7_out), .sel(LOGIC_B));

  // Notes on the sheet:
  //   SUB_AND: pull=down
  //   CC: pull=down
  //   Cin: pull=down
  //   SHL_XOR: pull=down
  //   LOGIC_B: pull=down
  //   B: pull=down
  //   A: pull=down
endmodule

module CMO_8x32_LED_matrix_driver (
  input  write_enable,
  input  [4:0] address,
  input  [7:0] write_data,
  input  clock,
  output [7:0] out_5,
  output [7:0] out_6,
  output [7:0] out_7,
  output [7:0] out_8,
  output [7:0] out_9,
  output [7:0] out_10,
  output [7:0] out_11,
  output [7:0] out_12,
  output [7:0] out_13,
  output [7:0] out_14,
  output [7:0] out_15,
  output [7:0] out_16,
  output [7:0] out_17,
  output [7:0] out_18,
  output [7:0] out_19,
  output [7:0] out_20,
  output [7:0] out_21,
  output [7:0] out_22,
  output [7:0] out_23,
  output [7:0] out_24,
  output [7:0] out_25,
  output [7:0] out_26,
  output [7:0] out_27,
  output [7:0] out_28,
  output [7:0] out_29,
  output [7:0] out_30,
  output [7:0] out_31,
  output [7:0] out_32,
  output [7:0] out_33,
  output [7:0] out_34,
  output [7:0] out_35,
  output [7:0] out_36
);

  wire demultiplexer_1_out0, demultiplexer_1_out1, demultiplexer_1_out2, demultiplexer_1_out3,
       demultiplexer_2_out0, demultiplexer_2_out1, demultiplexer_2_out2, demultiplexer_2_out3,
       demultiplexer_2_out4, demultiplexer_2_out5, demultiplexer_2_out6, demultiplexer_2_out7,
       demultiplexer_3_out0, demultiplexer_3_out1, demultiplexer_3_out2, demultiplexer_3_out3,
       demultiplexer_3_out4, demultiplexer_3_out5, demultiplexer_3_out6, demultiplexer_3_out7,
       demultiplexer_4_out0, demultiplexer_4_out1, demultiplexer_4_out2, demultiplexer_4_out3,
       demultiplexer_4_out4, demultiplexer_4_out5, demultiplexer_4_out6, demultiplexer_4_out7,
       demultiplexer_5_out0, demultiplexer_5_out1, demultiplexer_5_out2, demultiplexer_5_out3,
       demultiplexer_5_out4, demultiplexer_5_out5, demultiplexer_5_out6, demultiplexer_5_out7;

  Demultiplexer #(.select(2), .enable("false")) demultiplexer_1 (
    .out0(demultiplexer_1_out0), .out1(demultiplexer_1_out1), .out2(demultiplexer_1_out2),
    .out3(demultiplexer_1_out3), .in(write_enable), .sel(address[4:3]));
  Demultiplexer #(.select(3), .disabled(0), .enable("false")) demultiplexer_2 (
    .out0(demultiplexer_2_out0), .out1(demultiplexer_2_out1), .out2(demultiplexer_2_out2),
    .out3(demultiplexer_2_out3), .out4(demultiplexer_2_out4), .out5(demultiplexer_2_out5),
    .out6(demultiplexer_2_out6), .out7(demultiplexer_2_out7), .in(demultiplexer_1_out0), .sel(address[2:0]));
  Register register_1 (.D(write_data), .en(demultiplexer_2_out0), .Q(out_5), .clk(clock));  // open: clr
  Register register_2 (.D(write_data), .en(demultiplexer_2_out1), .Q(out_9), .clk(clock));  // open: clr
  Register register_3 (.D(write_data), .en(demultiplexer_2_out2), .Q(out_13), .clk(clock));  // open: clr
  Register register_4 (.D(write_data), .en(demultiplexer_2_out3), .Q(out_17), .clk(clock));  // open: clr
  Register register_5 (.D(write_data), .en(demultiplexer_2_out4), .Q(out_21), .clk(clock));  // open: clr
  Register register_6 (.D(write_data), .en(demultiplexer_2_out5), .Q(out_25), .clk(clock));  // open: clr
  Register register_7 (.D(write_data), .en(demultiplexer_2_out6), .Q(out_29), .clk(clock));  // open: clr
  Register register_8 (.D(write_data), .en(demultiplexer_2_out7), .Q(out_33), .clk(clock));  // open: clr
  Demultiplexer #(.select(3), .disabled(0), .enable("false")) demultiplexer_3 (
    .out0(demultiplexer_3_out0), .out1(demultiplexer_3_out1), .out2(demultiplexer_3_out2),
    .out3(demultiplexer_3_out3), .out4(demultiplexer_3_out4), .out5(demultiplexer_3_out5),
    .out6(demultiplexer_3_out6), .out7(demultiplexer_3_out7), .in(demultiplexer_1_out1), .sel(address[2:0]));
  Register register_9 (.D(write_data), .en(demultiplexer_3_out0), .Q(out_6), .clk(clock));  // open: clr
  Register register_10 (.D(write_data), .en(demultiplexer_3_out1), .Q(out_10), .clk(clock));  // open: clr
  Register register_11 (.D(write_data), .en(demultiplexer_3_out2), .Q(out_14), .clk(clock));  // open: clr
  Register register_12 (.D(write_data), .en(demultiplexer_3_out3), .Q(out_18), .clk(clock));  // open: clr
  Register register_13 (.D(write_data), .en(demultiplexer_3_out4), .Q(out_22), .clk(clock));  // open: clr
  Register register_14 (.D(write_data), .en(demultiplexer_3_out5), .Q(out_26), .clk(clock));  // open: clr
  Register register_15 (.D(write_data), .en(demultiplexer_3_out6), .Q(out_30), .clk(clock));  // open: clr
  Register register_16 (.D(write_data), .en(demultiplexer_3_out7), .Q(out_34), .clk(clock));  // open: clr
  Demultiplexer #(.select(3), .disabled(0), .enable("false")) demultiplexer_4 (
    .out0(demultiplexer_4_out0), .out1(demultiplexer_4_out1), .out2(demultiplexer_4_out2),
    .out3(demultiplexer_4_out3), .out4(demultiplexer_4_out4), .out5(demultiplexer_4_out5),
    .out6(demultiplexer_4_out6), .out7(demultiplexer_4_out7), .in(demultiplexer_1_out2), .sel(address[2:0]));
  Register register_17 (.D(write_data), .en(demultiplexer_4_out0), .Q(out_7), .clk(clock));  // open: clr
  Register register_18 (.D(write_data), .en(demultiplexer_4_out1), .Q(out_11), .clk(clock));  // open: clr
  Register register_19 (.D(write_data), .en(demultiplexer_4_out2), .Q(out_15), .clk(clock));  // open: clr
  Register register_20 (.D(write_data), .en(demultiplexer_4_out3), .Q(out_19), .clk(clock));  // open: clr
  Register register_21 (.D(write_data), .en(demultiplexer_4_out4), .Q(out_23), .clk(clock));  // open: clr
  Register register_22 (.D(write_data), .en(demultiplexer_4_out5), .Q(out_27), .clk(clock));  // open: clr
  Register register_23 (.D(write_data), .en(demultiplexer_4_out6), .Q(out_31), .clk(clock));  // open: clr
  Register register_24 (.D(write_data), .en(demultiplexer_4_out7), .Q(out_35), .clk(clock));  // open: clr
  Demultiplexer #(.select(3), .disabled(0), .enable("false")) demultiplexer_5 (
    .out0(demultiplexer_5_out0), .out1(demultiplexer_5_out1), .out2(demultiplexer_5_out2),
    .out3(demultiplexer_5_out3), .out4(demultiplexer_5_out4), .out5(demultiplexer_5_out5),
    .out6(demultiplexer_5_out6), .out7(demultiplexer_5_out7), .in(demultiplexer_1_out3), .sel(address[2:0]));
  Register register_25 (.D(write_data), .en(demultiplexer_5_out0), .Q(out_8), .clk(clock));  // open: clr
  Register register_26 (.D(write_data), .en(demultiplexer_5_out1), .Q(out_12), .clk(clock));  // open: clr
  Register register_27 (.D(write_data), .en(demultiplexer_5_out2), .Q(out_16), .clk(clock));  // open: clr
  Register register_28 (.D(write_data), .en(demultiplexer_5_out3), .Q(out_20), .clk(clock));  // open: clr
  Register register_29 (.D(write_data), .en(demultiplexer_5_out4), .Q(out_24), .clk(clock));  // open: clr
  Register register_30 (.D(write_data), .en(demultiplexer_5_out5), .Q(out_28), .clk(clock));  // open: clr
  Register register_31 (.D(write_data), .en(demultiplexer_5_out6), .Q(out_32), .clk(clock));  // open: clr
  Register register_32 (.D(write_data), .en(demultiplexer_5_out7), .Q(out_36), .clk(clock));  // open: clr
endmodule
